// Logisim project processor.circ as structural Verilog: 10 circuits, main circuit ul
module ul (
  input  [7:0] Input_1,
  input  [7:0] Input_2,
  output [7:0] Output_OR,
  output [7:0] Output_AND,
  output [7:0] Output_XOR
);

  assign Output_OR = Input_1 | Input_2;  // OR_Gate OR, 8 bits wide
  assign Output_AND = Input_1 & Input_2;  // AND_Gate AND, 8 bits wide
  assign Output_XOR = Input_2 ^ Input_1;  // XOR_Gate XOR, 8 bits wide
endmodule

module additionneur_1bit (
  input  An,
  input  Bn,
  input  Rin,
  output Sn,
  output Rout
);

  wire AND_2_out, AND_out, XOR_out;

  xor XOR (XOR_out, An, Bn);
  xor XOR_2 (Sn, XOR_out, Rin);
  and AND (AND_out, Rin, XOR_out);
  and AND_2 (AND_2_out, Bn, An);
  or OR (Rout, AND_out, AND_2_out);
endmodule

module additionneur_8bits (
  input  [7:0] A,
  input  [7:0] B,
  input  Rin,
  output [7:0] Output,
  output Rout
);

  wire additionneur_1bit_1_rout, additionneur_1bit_2_rout, additionneur_1bit_3_rout,
       additionneur_1bit_4_rout, additionneur_1bit_5_rout, additionneur_1bit_6_rout, additionneur_1bit_7_rout;

  additionneur_1bit additionneur_1bit_1 (
    .An(A[0]), .Bn(B[0]), .Rin(Rin), .Sn(Output[0]), .Rout(additionneur_1bit_1_rout));
  additionneur_1bit additionneur_1bit_2 (
    .An(A[1]), .Bn(B[1]), .Rin(additionneur_1bit_1_rout), .Sn(Output[1]), .Rout(additionneur_1bit_2_rout));
  additionneur_1bit additionneur_1bit_3 (
    .An(A[2]), .Bn(B[2]), .Rin(additionneur_1bit_2_rout), .Sn(Output[2]), .Rout(additionneur_1bit_3_rout));
  additionneur_1bit additionneur_1bit_4 (
    .An(A[3]), .Bn(B[3]), .Rin(additionneur_1bit_3_rout), .Sn(Output[3]), .Rout(additionneur_1bit_4_rout));
  additionneur_1bit additionneur_1bit_5 (
    .An(A[4]), .Bn(B[4]), .Rin(additionneur_1bit_4_rout), .Sn(Output[4]), .Rout(additionneur_1bit_5_rout));
  additionneur_1bit additionneur_1bit_6 (
    .An(A[5]), .Bn(B[5]), .Rin(additionneur_1bit_5_rout), .Sn(Output[5]), .Rout(additionneur_1bit_6_rout));
  additionneur_1bit additionneur_1bit_7 (
    .An(A[6]), .Bn(B[6]), .Rin(additionneur_1bit_6_rout), .Sn(Output[6]), .Rout(additionneur_1bit_7_rout));
  additionneur_1bit additionneur_1bit_8 (
    .An(A[7]), .Bn(B[7]), .Rin(additionneur_1bit_7_rout), .Sn(Output[7]), .Rout(Rout));

  // Notes on the sheet:
  //   S1
  //   S2
  //   S3
  //   S4
  //   S5
  //   S6
  //   S7
  //   S8
endmodule

module ual (
  input  [7:0] A,
  input  [7:0] in_2,
  input  [1:0] in_3,
  output [7:0] Output
);

  wire [7:0] additionneur_8bits_1_output, ul_1_output_or, ul_2_output_and, ul_3_output_xor;

  ul ul_1 (.Input_1(in_2), .Input_2(A), .Output_OR(ul_1_output_or));  // open: Output_AND, Output_XOR
  ul ul_2 (.Input_1(in_2), .Input_2(A), .Output_AND(ul_2_output_and));  // open: Output_OR, Output_XOR
  ul ul_3 (.Input_1(in_2), .Input_2(A), .Output_XOR(ul_3_output_xor));  // open: Output_OR, Output_AND
  additionneur_8bits additionneur_8bits_1 (
    .A(A), .B(in_2), .Rin(1'b0), .Output(additionneur_8bits_1_output));  // open: Rout
  Multiplexer #(.select(2), .width(8)) multiplexer_1 (
    .in0(ul_1_output_or), .in1(ul_2_output_and), .in2(ul_3_output_xor), .in3(additionneur_8bits_1_output),
    .out(Output), .sel(in_3));  // open: en

  // Notes on the sheet:
  //   B
  //   Rin
  //   OR
  //   AND
  //   XOR
  //   ADD
  //   Operation Selector
endmodule

module registre_8bits (
  input  Clock,
  input  [7:0] Input,
  input  in_3,
  output [7:0] Output
);

  D_Flip_Flop d_ff_1 (.clk(Clock), .D(Input[0]), .Q(Output[0]), .en(in_3));  // open: Qn, preset, reset
  D_Flip_Flop d_ff_2 (.clk(Clock), .D(Input[1]), .Q(Output[1]), .en(in_3));  // open: Qn, preset, reset
  D_Flip_Flop d_ff_3 (.clk(Clock), .D(Input[2]), .Q(Output[2]), .en(in_3));  // open: Qn, preset, reset
  D_Flip_Flop d_ff_4 (.clk(Clock), .D(Input[3]), .Q(Output[3]), .en(in_3));  // open: Qn, preset, reset
  D_Flip_Flop d_ff_5 (.clk(Clock), .D(Input[4]), .Q(Output[4]), .en(in_3));  // open: Qn, preset, reset
  D_Flip_Flop d_ff_6 (.clk(Clock), .D(Input[5]), .Q(Output[5]), .en(in_3));  // open: Qn, preset, reset
  D_Flip_Flop d_ff_7 (.clk(Clock), .D(Input[6]), .Q(Output[6]), .en(in_3));  // open: Qn, preset, reset
  D_Flip_Flop d_ff_8 (.clk(Clock), .D(Input[7]), .Q(Output[7]), .en(in_3));  // open: Qn, preset, reset
endmodule

module Banc_registre (
  input  Clock,
  input  [7:0] in_2,
  input  [1:0] in_3,
  input  [1:0] A_Selector,
  input  [1:0] B_Selector,
  output [7:0] Output_A,
  output [7:0] Output_B
);

  wire demultiplexer_1_out0, demultiplexer_1_out1, demultiplexer_1_out2, demultiplexer_1_out3;
  wire [7:0] registre_8bits_1_output, registre_8bits_2_output, registre_8bits_3_output,
       registre_8bits_4_output;

  Demultiplexer #(.select(2)) demultiplexer_1 (
    .out0(demultiplexer_1_out0), .out1(demultiplexer_1_out1), .out2(demultiplexer_1_out2),
    .out3(demultiplexer_1_out3), .in(1'b1), .sel(in_3));  // open: en
  registre_8bits registre_8bits_1 (
    .Clock(Clock), .Input(in_2), .in_3(demultiplexer_1_out0), .Output(registre_8bits_1_output));
  registre_8bits registre_8bits_2 (
    .Clock(Clock), .Input(in_2), .in_3(demultiplexer_1_out1), .Output(registre_8bits_2_output));
  registre_8bits registre_8bits_3 (
    .Clock(Clock), .Input(in_2), .in_3(demultiplexer_1_out2), .Output(registre_8bits_3_output));
  registre_8bits registre_8bits_4 (
    .Clock(Clock), .Input(8'h1), .in_3(demultiplexer_1_out3), .Output(registre_8bits_4_output));
  Multiplexer #(.select(2), .width(8)) multiplexer_1 (
    .in0(registre_8bits_1_output), .in1(registre_8bits_2_output), .in2(registre_8bits_3_output),
    .in3(registre_8bits_4_output), .out(Output_A), .sel(A_Selector));  // open: en
  Multiplexer #(.select(2), .width(8)) multiplexer_2 (
    .in0(registre_8bits_1_output), .in1(registre_8bits_2_output), .in2(registre_8bits_3_output),
    .in3(registre_8bits_4_output), .out(Output_B), .sel(B_Selector));  // open: en

  // Notes on the sheet:
  //   Input
endmodule

module CPU (
  input  Clock,
  input  [1:0] Choice_Register,
  input  [1:0] Output_A_Selector,
  input  [1:0] Operation_Selector,
  input  [1:0] Output_B_selector,
  input  [7:0] Load_Store_Values,
  input  Load_Store,
  output [7:0] Output
);

  wire [7:0] banc_registre_1_output_a, banc_registre_1_output_b, UAL_output;

  Banc_registre banc_registre_1 (
    .Clock(Clock), .in_2(Output), .in_3(Choice_Register), .A_Selector(Output_A_Selector),
    .B_Selector(Output_B_selector), .Output_A(banc_registre_1_output_a), .Output_B(banc_registre_1_output_b));
  ual UAL (
    .A(banc_registre_1_output_a), .in_2(banc_registre_1_output_b), .in_3(Operation_Selector),
    .Output(UAL_output));
  Multiplexer #(.width(8)) multiplexer_1 (
    .in0(UAL_output), .in1(Load_Store_Values), .out(Output), .sel(Load_Store));  // open: en
endmodule

module PC (
  input  Reset,
  output [7:0] Output,
  output [7:0] out_3,
  output [1:0] Choice_Register,
  output [1:0] A_Selector,
  output [1:0] out_6,
  output [1:0] B_Selector
);

  wire clock_1_out;
  wire [7:0] Counter_q;

  Counter Counter (.Q(Counter_q), .clk(clock_1_out), .clr(Reset));  // open: load, D, count, carry
  ROM rom_1 (.addr(Counter_q), .data(out_3));  // open: sel
  decodage decodage_1 (.in_1(out_3), .out_2(Choice_Register), .out_3(A_Selector), .out_4(out_6), .out_5(B_Selector));
  Clock clock_1 (.out(clock_1_out));
  CPU CPU (
    .Clock(clock_1_out), .Choice_Register(Choice_Register), .Output_A_Selector(A_Selector),
    .Operation_Selector(out_6), .Output_B_selector(B_Selector), .Output(Output));  // open: Load_Store_Values, Load_Store

  // Notes on the sheet:
  //   contents of rom_1 (hex, n*v repeats v):
  //   f3 15*3c
  //   Splitter
  //   Operationr Selector
endmodule

module decodage (
  input  [7:0] in_1,
  output [1:0] out_2,
  output [1:0] out_3,
  output [1:0] out_4,
  output [1:0] out_5
);


  assign out_2 = in_1[7:6];
  assign out_3 = in_1[5:4];
  assign out_4 = in_1[3:2];
  assign out_5 = in_1[1:0];
endmodule

module PC_with_RAM (
  input  in_1,
  input  Clock,
  output [1:0] out_3,
  output [1:0] out_4,
  output [1:0] out_5,
  output [1:0] out_6,
  output [17:0] out_7,
  output Load,
  output [7:0] Data,
  output [7:0] RAM,
  output Store,
  output [7:0] Load_Store_Value
);

  wire clock_1_out, not_1_out;
  wire [7:0] Counter_q;

  Counter Counter (.Q(Counter_q), .clk(clock_1_out), .clr(in_1));  // open: load, D, count, carry
  ROM #(.dataWidth(18)) rom_1 (.addr(Counter_q), .data({out_7[17:9], Load, out_3, out_4, out_5, out_6}));  // open: sel
  not not_1 (not_1_out, out_7[9]);
  Clock clock_1 (.out(clock_1_out));
  CPU CPU (
    .Clock(clock_1_out), .Choice_Register(out_3), .Output_A_Selector(out_4), .Operation_Selector(out_5),
    .Output_B_selector(out_6), .Load_Store_Values(Load_Store_Value), .Load_Store(Load), .Output(Data));
  RAM ram_1 (.addr(out_7[17:10]), .data(Load_Store_Value), .clk(Clock), .ld(not_1_out));  // open: sel, clr
  assign Load_Store_Value = Data;  // Buffer buffer_1, 8 bits wide

  assign out_7[8:0] = {Load, out_3, out_4, out_5, out_6};
  assign RAM = out_7[17:10];
  assign Store = out_7[9];

  // Notes on the sheet:
  //   contents of rom_1 (hex, n*v repeats v):
  //   f3 6f3 500 13 3213
endmodule
